# Fritzing sketch LM358 (saved by Fritzing 0.9.3b)
breadboards: 1

parts:
  LED1 = smd LED [color="Red (633nm)" package="0805 [SMD]"]  # not connected
  U3 = POT_SWITCH [package=pot_pth]
  R8 = Resistor [tolerance=±5% resistance=220 package="1206 [SMD]"]
  VCC1 = Battery block 9V
  U4 = LM358 [package=dip08]
  R9 = Resistor [tolerance=±5% resistance=220 package="1206 [SMD]"]
  P1 = S1133 Si Photodiode [package="8mm Ceramic [THT]"]
  Q1 = LTR-301 [package=ltr-301]
  R10 = Resistor [tolerance=±5% resistance=220 package="1206 [SMD]"]

nets:
  N1: U3.G$2_1, U4.G$1_-IN
  N2: U3.G$1_E, R9.Pin_0
  N3: R8.Pin_0, VCC1.-, VCC1.+, P1.cathode, Q1.E, R10.Pin_0
  N4: U4.G$1_+IN, R9.Pin_1, P1.anode
  N5: Q1.C, R10.Pin_1
