# Fritzing sketch LM393 (saved by Fritzing 0.9.3b)
breadboards: 1

parts:
  IC1 = Dual Op-Amp [package=dip08]
  LED1 = smd LED [color="Red (633nm)" package="0805 [SMD]"]  # not connected
  R1 = Resistor [tolerance=±5% resistance=220 package="1206 [SMD]"]
  R2 = Rotary Potentiometer (Small) [maximum_resistance=100kΩ package=THT]
  C1 = Capacitor [package=cap-pth-small2]
  R3 = Resistor [tolerance=±5% resistance=220 package="1206 [SMD]"]
  R4 = Resistor [tolerance=±5% resistance=220 package="1206 [SMD]"]
  R5 = Resistor [tolerance=±5% resistance=220 package="1206 [SMD]"]
  R6 = Resistor [tolerance=±5% resistance=220 package="1206 [SMD]"]  # not connected
  LED2 = smd LED [color="Red (633nm)" package="0805 [SMD]"]
  R7 = Resistor [tolerance=±5% resistance=220 package="1206 [SMD]"]
  C2 = Capacitor [package=cap-pth-small2]
  BAT1 = BC9VPC [package=bc9vpc]

nets:
  N1: IC1.A_OUT, R1.Pin_1
  N2: IC1.A_-IN, R2.wiper
  N3: IC1.A_+IN, C1.1, R3.Pin_1, R4.Pin_0
  N4: IC1.A_V-, R2.leg2, C1.2, R4.Pin_1, R5.Pin_0, C2.1, BAT1.V-
  N5: IC1.A_V+, R2.leg1, R3.Pin_0, LED2.anode, R7.Pin_0, C2.2, BAT1.V+
  N6: R1.Pin_0, R7.Pin_1
  N7: R5.Pin_1, LED2.cathode
