# Fritzing sketch NE555 (saved by Fritzing 0.9.3b)
breadboards: 1

parts:
  U1 = 555 Timer [package="DIP8 [THT]"]
  R1 = Photocell (LDR) [package=THT]
  R2 = Resistor [tolerance=±5% resistance=220 package="0603 [SMD]"]
  U2 = TRANSISTOR_NPN_2 [package=to-92]
  C1 = Capacitor [package=cap-pth-small2]
  U3 = RELAY [package=relay-g5q]
  M1 = DC Motor
  VCC1 = Battery block 9V
  U4 = TRANSISTOR_NPN_2 [package=to-92]
  R3 = Resistor [tolerance=±5% resistance=220 package="0603 [SMD]"]
  U5 = TRANSISTOR_NPN_2 [package=to-92]
  R4 = Resistor [tolerance=±5% resistance=220 package="0603 [SMD]"]
  R5 = Resistor [tolerance=±5% resistance=220 package="0603 [SMD]"]
  C2 = Capacitor [package=cap-pth-small2]
  R6 = Resistor [tolerance=±5% resistance=220 package="0603 [SMD]"]
  R7 = Resistor [tolerance=±5% resistance=220 package="0603 [SMD]"]

nets:
  N1: U1.Ground, U2.C, C1.2, M1.pin_1, VCC1.-, U4.C, C2.2
  N2: U1.Trigger, U5.C
  N3: U1.Output, U2.E
  N4: U1.Reset, U1.Vcc_Supply_Voltage, R1.pin_0, U3.MAIN, U3.COIL1, VCC1.+, R4.Pin_1, R5.Pin_1, R7.Pin_1
  N5: U1.Control_Voltage, C1.1
  N6: U1.Threshold, C2.1, R6.Pin_0
  N7: U1.Discharge, R6.Pin_1, R7.Pin_0
  N8: R1.pin_1, R2.Pin_0
  N9: R2.Pin_1, U4.E
  N10: U2.B, U3.COIL2
  N11: U4.B, R3.Pin_1, R4.Pin_0
  N12: R3.Pin_0, U5.E
  N13: U5.B, R5.Pin_0
