# Fritzing sketch SCR (saved by Fritzing 0.9.3b)
breadboards: 1

parts:
  U1 = TRIAC [package=to-92]
  LED1 = smd LED [color="Red (633nm)" package="0603 [SMD]"]
  C2 = Electrolytic Capacitor [capacitance=100μF package="0807 [SMD, electrolytic]"]
  R1 = Resistor [tolerance=±5% resistance=220 package="0805 [SMD]"]
  S2 = Square Pushbutton
  S3 = SWITCH-MOMENTARY-2 [package=reed_switch_pth]
  R2 = Resistor [tolerance=±5% resistance=220 package="0805 [SMD]"]
  R3 = Resistor [tolerance=±5% resistance=220 package="0805 [SMD]"]
  R4 = Resistor [tolerance=±5% resistance=220 package="0805 [SMD]"]
  J1 = Piezo Speaker
  VCC1 = 4 x AAA Battery Mount

nets:
  N1: U1.M1, S2.leg0, R2.Pin_1, VCC1.-
  N2: U1.G, C2.-, R3.Pin_0, J1.pin1
  N3: U1.M2, R1.Pin_1, R2.Pin_0
  N4: LED1.cathode, R3.Pin_1
  N5: LED1.anode, S3.2, R4.Pin_0, J1.pin2, VCC1.+
  N6: C2.+, S2.leg1
  N7: R1.Pin_0, S3.1

notes:
  Thay thế cảm biến rung
